# Fritzing sketch Student_Node_Diagram (saved by Fritzing 0.9.3b)
breadboards: 1

parts:
  Part1 = Arduino Micro (Rev3)  # not connected
  U1 = XBee
  S1 = Pushbutton [package="[THT]"]
  LED1 = smd LED [color="Green (555nm)" package="1206 [SMD]"]  # not connected
  R1 = Resistor [tolerance=±5% resistance=1k package=THT]  # not connected

nets:
  N1: U1.GND, S1.Pin_1, S1.Pin_2
  N2: S1.Pin_3, S1.Pin_4
