# Fritzing sketch Teacher_Node_Diagram (saved by Fritzing 0.9.3b)
breadboards: 1

parts:
  Part1 = Arduino Micro (Rev3)  # not connected
  U1 = XBee
  S1 = Pushbutton [package="[THT]"]

nets:
  N1: U1.GND, S1.Pin_1, S1.Pin_2
  N2: S1.Pin_3, S1.Pin_4
